// Logisim project 1818965_Simple fire Alarm system.circ as structural Verilog: 1 circuit, main circuit main
module main (
  input  in_1,
  input  in_2,
  input  in_3,
  input  in_4,
  input  in_5,
  output out_6,
  output out_7
);

  wire and_1_out, and_2_out;

  and and_1 (and_1_out, in_1, in_2);
  and and_2 (and_2_out, in_3, in_5);
  or or_1 (out_6, and_1_out, and_2_out);
  or or_2 (out_7, out_6, in_4);
endmodule
